# Fritzing sketch OpenBot (saved by Fritzing 0.9.3b)

parts:
  M2 = DC Motor
  S1 = H-Bridge with L298N
  M3 = DC Motor
  S2 = Pololu QTR-8 Reflectabce Sensor array [package=THT]
  U1 = SWITCH_SPDT [package=kps-1290]
  Part2 = FC-03 [chip_label=FC-03]
  Part3 = FC-03 [chip_label=FC-03]
  Part1 = Arduino Uno (Rev3)
  VCC1 = 4 x AAA Battery Mount
  VCC2 = 4 x AAA Battery Mount
  U2 = SWITCH_SPDT [package=kps-1290]
  hc-sr1 = hc-sr04
  J1 = Basic Servo
  LED1 = smd LED [color="Red (633nm)" package="0603 [SMD]"]

nets:
  N1: M2.pin_1, S1.M1-02
  N2: M2.pin_2, S1.M1-01
  N3: S1.12V, U2.P
  GND: S1.GND, S2.pin1, S2.pin15, Part1.GND, VCC1.-, VCC2.-
  N4: S1.ENA, Part1.D9_PWM
  N5: S1.IN1, Part1.D4
  N6: S1.IN2, Part1.D5_PWM
  N7: S1.IN3, Part1.D7
  N8: S1.IN4, Part1.D6_PWM
  N9: S1.ENB, Part1.D10_PWM/SS
  N10: S1.M2-01, M3.pin_2
  N11: S1.M2-02, M3.pin_1
  N12: S2.pin2, Part1.5V
  N13: S2.pin4, S2.pin6, Part1.A5/SCL
  N14: S2.pin7, Part1.A4/SDA
  N15: S2.pin8, Part1.A3
  N16: S2.pin9, Part1.A2
  N17: S2.pin10, Part1.A1
  N18: S2.pin11, Part1.A0
  N19: U1.P, Part1.VIN
  N20: Part2.pin_2, J1.gnd
  N21: Part2.pin_3, Part1.D3_PWM
  N22: Part3.pin_1, J1.vcc
  N23: Part3.pin_3, Part1.D2
  N24: Part1.D8, hc-sr1.Trig
  N25: Part1.D11_PWM/MOSI, J1.pulse
  N26: Part1.D12/MISO, hc-sr1.Echo
  N27: Part1.D13/SCK, LED1.anode

notes:
  In the scheamtic we will use 2 single switches. In reality there will be 1 double switch.
  left motor
  right motor

custom parts:
  H-Bridge with L298N: h-bridge
  FC-03: FC-03, LM393 IR Speed Sensor Encoder
